# Fritzing sketch Analog Sketch (saved by Fritzing 0.9.2b)
breadboards: 1

parts:
  Raspberry_Pi1 = Raspberry Pi 2
  J1 = Cobbler Plus Cable
  U1 = TMP36 [package=to-92]
  IC1 = ADS1115 16-bit ADC Breakout

nets:
  3V3: Raspberry_Pi1.3v3, Raspberry_Pi1.3V3, J1.3.3V#41, J1.3.3V#57
  N1: Raspberry_Pi1.GPIO2, J1.GPIO_2
  N2: Raspberry_Pi1.GPIO3, J1.GPIO_3
  N3: Raspberry_Pi1.GPIO4, J1.GPIO_4
  N4: Raspberry_Pi1.GND, J1.GND#46, J1.GND#49, J1.GND#54, J1.GND#60, J1.GND#65, J1.GND#70, J1.GND#74, J1.GND#79
  N5: Raspberry_Pi1.GPIO17, J1.GPIO_17
  N6: Raspberry_Pi1.GPIO27, J1.GPIO_27
  N7: Raspberry_Pi1.GPIO22, J1.GPIO_22
  N8: Raspberry_Pi1.GPIO10, J1.GPIO_10
  N9: Raspberry_Pi1.GPIO9, J1.GPIO_9
  N10: Raspberry_Pi1.GPIO11, J1.GPIO_11
  N11: Raspberry_Pi1.ID_SD, J1.ID_SD
  N12: Raspberry_Pi1.GPIO5, J1.GPIO_5
  N13: Raspberry_Pi1.GPIO6, J1.GPIO_6
  N14: Raspberry_Pi1.GPIO13, J1.GPIO_13
  N15: Raspberry_Pi1.GPIO19, J1.GPIO_19
  N16: Raspberry_Pi1.GPIO26, J1.GPIO_26
  N17: Raspberry_Pi1.GPIO21, J1.GPIO_21
  N18: Raspberry_Pi1.GPIO20, J1.GPIO_20
  N19: Raspberry_Pi1.GPIO16, J1.GPIO_16
  N20: Raspberry_Pi1.GPIO12, J1.GPIO_12
  N21: Raspberry_Pi1.ID_SC, J1.ID_SC
  N22: Raspberry_Pi1.GPIO7, J1.GPIO_7
  N23: Raspberry_Pi1.GPIO8, J1.GPIO_8
  N24: Raspberry_Pi1.GPIO25, J1.GPIO_25
  N25: Raspberry_Pi1.GPIO24, J1.GPIO_24
  N26: Raspberry_Pi1.GPIO23, J1.GPIO_23
  N27: Raspberry_Pi1.GPIO18, J1.GPIO_18
  N28: Raspberry_Pi1.GPIO15, J1.GPIO_15
  N29: Raspberry_Pi1.GPIO14, J1.GPIO_14
  5V: Raspberry_Pi1.5V, J1.5V
  3V3_2: J1.3V3, IC1.VDD
  N30: J1.5.0V#1, U1.VCC
  N31: J1.SDA, IC1.SDA
  N32: J1.SCL, IC1.SCL
  GND: J1.GND#8, U1.GND, IC1.GND, IC1.ADDR
  N33: J1.#27, IC1.ALRT
  N34: U1.VOUT, IC1.A0

custom parts:
  Cobbler Plus Cable: The Cobbler Plus is an add on prototyping board from Adafruit specifically designed for the Raspberry Pi B+ that can break out all those tasty power, GPIO, I2C and SPI pins from the 40-pin header onto a solderless breadboard. This set will make "cobbling together" prototypes with the Pi super easy. The Cobbler Plus can plug into any solderless breadboard.
  ADS1115 16-bit ADC Breakout: ADS1015 12-bit I2C ADC+PGA Breakout
